# Fritzing sketch mainboard (saved by Fritzing 0.9.3b)
circuit board: 7.80366cm x 6.58223cm
circuit board: 2.5cm x 3.5cm
circuit board: 3cm x 6.5cm
breadboards: 1

parts:
  Nano = Arduino Nano (Rev3.0)
  Q1 = PNP-Transistor [package="TO92 [THT]"]
  1000C = mystery part, 8 pins [chip_label=?]
  Q2 = PNP-Transistor [package="TO92 [THT]"]
  Q3 = NPN-Transistor [package="TO92 [THT]"]
  Q4 = NPN-Transistor [package="TO92 [THT]"]
  D1 = Rectifier Diode [part_number=1N4001 package="300 mil [THT]"]
  D2 = Rectifier Diode [part_number=1N4001 package="300 mil [THT]"]
  D3 = Rectifier Diode [part_number=1N4001 package="300 mil [THT]"]
  D4 = Rectifier Diode [part_number=1N4001 package="300 mil [THT]"]
  R1 = Resistor [tolerance=±5% resistance=10k package=THT]
  R3 = Resistor [tolerance=±5% resistance=10k package=THT]
  R4 = Resistor [tolerance=±5% resistance=10k package=THT]
  R2 = Resistor [tolerance=±5% resistance=10k package=THT]
  J1 = female pin header, 2 pins [form="♀ (female)"]
  Q5 = PNP-Transistor [package="TO92 [THT]"]
  Q6 = PNP-Transistor [package="TO92 [THT]"]
  Q7 = NPN-Transistor [package="TO92 [THT]"]
  Q8 = NPN-Transistor [package="TO92 [THT]"]
  D8 = Rectifier Diode [part_number=1N4001 package="300 mil [THT]"]
  D6 = Rectifier Diode [part_number=1N4001 package="300 mil [THT]"]
  D5 = Rectifier Diode [part_number=1N4001 package="300 mil [THT]"]
  D7 = Rectifier Diode [part_number=1N4001 package="300 mil [THT]"]
  R8 = Resistor [tolerance=±5% resistance=10k package=THT]
  R6 = Resistor [tolerance=±5% resistance=10k package=THT]
  R7 = Resistor [tolerance=±5% resistance=10k package=THT]
  R5 = Resistor [tolerance=±5% resistance=10k package=THT]
  J2 = female pin header, 2 pins [form="♀ (female)"]
  Shutdown = Pushbutton [package="[THT]"]
  Power = Toggle Switch [package=THT]
  MinUMU9v5 = mystery part, 5 pins [chip_label=?]
  C1 = Electrolytic Capacitor [capacitance=1µF package="100 mil [THT, electrolytic]"]
  C2 = Ceramic Capacitor [capacitance=100nF package="100 mil [THT, multilayer]"]
  USB = USB Connectors [package=usb-minib-nostop]  # not connected
  JST = Header 2 [package=jst-2-smd]  # not connected
  POWER = USB Connectors [package=usb-minib-nostop]  # not connected
  USB_2 = USB Connectors [package=usb-minib-nostop]  # not connected
  HDMI = USB+SHIELD [package=usb-b-pth]  # not connected
  J3 = female pin header, 3 pins [form="♀ (female)"]
  J5 = Generic double row male header - 40 pins [form="♂ (male)" package=THT]
  J4 = female pin header, 3 pins [form="♀ (female)"]

nets:
  N1: Nano.GND, 1000C.pin8, Q3.E, Q4.E, D3.anode, D4.anode, Q7.E, Q8.E, D8.anode, D7.anode, Shutdown.Pin_1, Shutdown.Pin_2, Shutdown.Pin_3, Shutdown.Pin_4, Power.COM, Power.L2, C1.-, C2.0, J3.pin2, J5.pin39, J5.pin38, J5.pin4, J4.pin2
  N2: Nano.D2, J4.pin1
  N3: Nano.D3, J3.pin1
  N4: Nano.D5, R1.Pin_1, R3.Pin_0
  N5: Nano.D6, R4.Pin_0, R2.Pin_1
  N6: Nano.D9, R7.Pin_0, R5.Pin_1
  N7: Nano.D10, R8.Pin_0, R6.Pin_1
  N8: Nano.VIN, Q1.E, 1000C.pin7, Q2.E, D1.cathode, D2.cathode, Q5.E, Q6.E, D6.cathode, D5.cathode, C1.+, C2.1, J3.pin3, J5.pin6, J4.pin3
  N9: Nano.A5, MinUMU9v5.pin1, J5.pin5
  N10: Nano.A4, MinUMU9v5.pin2, J5.pin3
  N11: Q1.B, R1.Pin_0
  N12: Q1.C, Q3.C, D1.anode, D3.cathode, J1.pin2
  N13: 1000C.pin4, Power.L1
  N14: Q2.B, R2.Pin_0
  N15: Q2.C, Q4.C, D2.anode, D4.cathode, J1.pin1
  N16: Q3.B, R3.Pin_1
  N17: Q4.B, R4.Pin_1
  N18: Q5.B, R5.Pin_0
  N19: Q5.C, Q7.C, D5.anode, D7.cathode, J2.pin2
  N20: Q6.B, R6.Pin_0
  N21: Q6.C, Q8.C, D8.cathode, D6.anode, J2.pin1
  N22: Q7.B, R7.Pin_1
  N23: Q8.B, R8.Pin_1
  N24: MinUMU9v5.pin3, J5.pin20
  N25: MinUMU9v5.pin5, J5.pin17

custom parts:
  Generic double row male header - 40 pins: Generic double row male header
